// Logisim project adder.circ as structural Verilog: 6 circuits, main circuit main
module main (
  input  [31:0] A,
  input  [31:0] B,
  input  sub,
  output ovf,
  output [31:0] result
);

  wire _16_bit_c_out, n16bitaddersub_1_c_out;
  wire [15:0] bit_extender_1_out, XOR_2_out, XOR_out;

  assign bit_extender_1_out = {{15{sub}}, sub};  // Bit_Extender bit_extender_1
  assign XOR_out = bit_extender_1_out ^ B[15:0];  // XOR_Gate XOR, 16 bits wide
  _16BitAdderSub _16_bit (.A(A[15:0]), .B(XOR_out), .c_in(sub), .c_out(_16_bit_c_out), .result(result[15:0]));
  assign XOR_2_out = bit_extender_1_out ^ B[31:16];  // XOR_Gate XOR_2, 16 bits wide
  _16BitAdderSub u_16bitaddersub_1 (
    .A(A[31:16]), .B(XOR_2_out), .c_in(_16_bit_c_out), .c_out(n16bitaddersub_1_c_out), .result(result[31:16]));
  nor nor_1 (ovf, n16bitaddersub_1_c_out, _16_bit_c_out);

  // Notes on the sheet:
  //   32-Bit Adder/Subtractor
endmodule

module FullAdder (
  input  A,
  input  B,
  input  sub,
  output result,
  output ovf
);

  wire halfadder_1_carry, halfadder_1_result, halfadder_2_carry;

  HalfAdder halfadder_1 (.A(A), .B(B), .result(halfadder_1_result), .carry(halfadder_1_carry));
  HalfAdder halfadder_2 (.A(halfadder_1_result), .B(sub), .result(result), .carry(halfadder_2_carry));
  or or_1 (ovf, halfadder_2_carry, halfadder_1_carry);

  // Notes on the sheet:
  //   Full Adder
  //   c1
  //   s1
  //   s2
  //   c2
endmodule

// HA
module HalfAdder (
  input  A,
  input  B,
  output result,
  output carry
);

  xor xor_1 (result, A, B);
  and and_1 (carry, A, B);

  // Notes on the sheet:
  //   Binary Half Adder
endmodule

module _16BitAdderSub (
  input  [15:0] A,
  input  [15:0] B,
  input  c_in,
  output c_out,
  output [15:0] result
);

  wire _4_bit_c_out, n4add_1_c_out, n4add_2_c_out;

  _4Add _4_bit (.A(B[3:0]), .B(A[3:0]), .C_in(c_in), .c_out(_4_bit_c_out), .result(result[3:0]));
  _4Add u_4add_1 (.A(B[7:4]), .B(A[7:4]), .C_in(_4_bit_c_out), .c_out(n4add_1_c_out), .result(result[7:4]));
  _4Add u_4add_2 (.A(B[11:8]), .B(A[11:8]), .C_in(n4add_1_c_out), .c_out(n4add_2_c_out), .result(result[11:8]));
  _4Add u_4add_3 (.A(B[15:12]), .B(A[15:12]), .C_in(n4add_2_c_out), .c_out(c_out), .result(result[15:12]));

  // Notes on the sheet:
  //   C0
  //   16-Bit Adder/Subtractor
  //   C1
  //   C2
  //   C3
endmodule

module _4Add (
  input  [3:0] A,
  input  [3:0] B,
  input  C_in,
  output c_out,
  output [3:0] result
);

  wire full_1_carryout, full_2_carryout, full_3_carryout;

  Full full_1 (.carryIn(C_in), .A(A[0]), .B(B[0]), .result(result[0]), .carryOut(full_1_carryout));
  Full full_2 (.carryIn(full_1_carryout), .A(A[1]), .B(B[1]), .result(result[1]), .carryOut(full_2_carryout));
  Full full_3 (.carryIn(full_2_carryout), .A(A[2]), .B(B[2]), .result(result[2]), .carryOut(full_3_carryout));
  Full full_4 (.carryIn(full_3_carryout), .A(A[3]), .B(B[3]), .result(result[3]), .carryOut(c_out));

  // Notes on the sheet:
  //   C0
  //   4 bit adder
  //   C1
  //   C2
  //   C3
endmodule

module Full (
  input  carryIn,
  input  A,
  input  B,
  output result,
  output carryOut
);

  wire and_1_out, and_2_out, xor_1_out;

  xor xor_1 (xor_1_out, A, B);
  and and_1 (and_1_out, A, B);
  xor xor_2 (result, xor_1_out, carryIn);
  and and_2 (and_2_out, carryIn, xor_1_out);
  or or_1 (carryOut, and_2_out, and_1_out);

  // Notes on the sheet:
  //   Full Adder
endmodule
