// Logisim project circuit2.circ as structural Verilog: 1 circuit, main circuit main
module main (
  input  A,
  input  B,
  input  C,
  output out1,
  output out2
);

  wire A_nB_C_out, nA_B_C_out, nA_nB_2_out, nA_nB_nC_out, nA_nB_out, not_1_out, not_2_out, not_3_out;

  not not_1 (not_1_out, A);
  not not_2 (not_2_out, C);
  not not_3 (not_3_out, B);
  and A_nB_C (A_nB_C_out, A, C, not_3_out);
  and nA_nB (nA_nB_out, not_3_out, not_1_out);
  and nA_nB_2 (nA_nB_2_out, not_1_out, not_2_out);
  and nA_nB_nC (nA_nB_nC_out, not_1_out, not_3_out, not_2_out);
  and nA_B_C (nA_B_C_out, B, C, not_1_out);
  or nB_nC___B_C___A_nB_C (out1, A_nB_C_out, nA_nB_nC_out, nA_B_C_out);
  or or_1 (out2, nA_nB_out, nA_nB_2_out);
endmodule
