// Logisim project fsm.circ as structural Verilog: 6 circuits, main circuit main
module main (
  input  in1,
  input  in2,
  input  in3,
  output out1,
  output out2
);

  wire clock_1_out, out1_1_out, out2d0_both_1_out, out2d1_1_out_6, Q0_q;

  out1 out1_1 (.A(in1), .B(in2), .C(in3), .out(out1_1_out));
  out2D1 out2d1_1 (.A(in1), .B(in2), .C(in3), .Q1(out2), .Q0(Q0_q), .out_6(out2d1_1_out_6));
  out2D0_both out2d0_both_1 (.A(in1), .B(in2), .C(in3), .Q1(out2), .Q0(Q0_q), .out(out2d0_both_1_out));
  Clock clock_1 (.out(clock_1_out));
  D_Flip_Flop d_ff_1 (.clk(clock_1_out), .D(out1_1_out), .Q(out1));  // open: Qn, preset, en, reset
  D_Flip_Flop Q1 (.clk(clock_1_out), .D(out2d1_1_out_6), .Q(out2));  // open: Qn, preset, en, reset
  D_Flip_Flop Q0 (.clk(clock_1_out), .D(out2d0_both_1_out), .Q(Q0_q));  // open: Qn, preset, en, reset
endmodule

module out1 (
  input  A,
  input  B,
  input  C,
  output out
);

  wire A__B_xor_C_out, B_C_out, B_xor_C_out;

  xor B_xor_C (B_xor_C_out, B, C);
  and B_C (B_C_out, B, C);
  and A__B_xor_C (A__B_xor_C_out, B_xor_C_out, A);
  or or_1 (out, A__B_xor_C_out, B_C_out);
endmodule

module out2D0_xor (
  input  A,
  input  B,
  input  C,
  input  Q1,
  input  Q0,
  output out
);

  wire A_B_out, A_nB_nC_out, B_xnor_C_out, nA__B_xor_C_out, not_1_out, not_2_out, or_1_out, xor_1_out;

  not not_1 (not_1_out, A);
  not not_2 (not_2_out, B);
  xnor B_xnor_C (B_xnor_C_out, C, B);
  and A_nB_nC (A_nB_nC_out, not_2_out, C, A);
  and nA__B_xor_C (nA__B_xor_C_out, not_1_out, B_xnor_C_out);
  and A_B (A_B_out, A, B);
  or or_1 (or_1_out, A_B_out, nA__B_xor_C_out, A_nB_nC_out);
  xor xor_1 (xor_1_out, Q1, Q0);
  and and_1 (out, or_1_out, xor_1_out);
endmodule

// out2circ
module out2D0_both (
  input  A,
  input  B,
  input  C,
  input  Q1,
  input  Q0,
  output out
);

  wire out2d0_xnor_1_out, out2d0_xor_1_out;

  out2D0_xor out2d0_xor_1 (.A(A), .B(B), .C(C), .Q1(Q1), .Q0(Q0), .out(out2d0_xor_1_out));
  out2D0_xnor out2d0_xnor_1 (.A(A), .B(B), .C(C), .Q1(Q1), .Q0(Q0), .out(out2d0_xnor_1_out));
  or \or  (out, out2d0_xor_1_out, out2d0_xnor_1_out);
endmodule

module out2D0_xnor (
  input  A,
  input  B,
  input  C,
  input  Q1,
  input  Q0,
  output out
);

  wire A_nB_nC_out, B_xor_C_out, nA__B_xor_C_out, not_1_out, not_2_out, not_3_out, or_1_out, Q1_xnor_Q0_out;

  not not_1 (not_1_out, B);
  not not_2 (not_2_out, A);
  xor B_xor_C (B_xor_C_out, B, C);
  not not_3 (not_3_out, C);
  and nA__B_xor_C (nA__B_xor_C_out, not_2_out, B_xor_C_out);
  and A_nB_nC (A_nB_nC_out, not_3_out, not_1_out, A);
  or or_1 (or_1_out, nA__B_xor_C_out, A_nB_nC_out);
  xnor Q1_xnor_Q0 (Q1_xnor_Q0_out, Q1, Q0);
  and and_1 (out, or_1_out, Q1_xnor_Q0_out);
endmodule

// out1circ
module out2D1 (
  input  A,
  input  B,
  input  C,
  input  Q1,
  input  Q0,
  output out_6
);

  wire A_B_out, A_nB_nC_out, nA_B_C_out, nA_nB_out, nB_C_out, not_1_out, not_2_out, not_3_out, or_1_out,
       xor_out;

  not not_1 (not_1_out, A);
  and A_B (A_B_out, A, B);
  not not_2 (not_2_out, B);
  not not_3 (not_3_out, C);
  and nA_nB (nA_nB_out, not_1_out, not_3_out);
  and nB_C (nB_C_out, not_2_out, C);
  xor \xor  (xor_out, Q1, Q0);
  and A_nB_nC (A_nB_nC_out, A, not_2_out, not_3_out);
  and nA_B_C (nA_B_C_out, not_1_out, B, C);
  or or_1 (or_1_out, nA_nB_out, A_nB_nC_out, A_B_out, nA_B_C_out, nB_C_out);
  and and_1 (out_6, or_1_out, xor_out);
endmodule
