// Logisim project hw4.circ as structural Verilog: 13 circuits, main circuit main
// rdst
module main (
  input  reset
);

  wire ALUbit1, ALUbit2, ALUbit3, clk, comparator_1_gt, comparator_2_eq, DMRE, DMWE, Imm, \input , jal,
       keyboard_1_avail, not_1_out, not_3_out, \output , Rdst, WE;
  wire [2:0] multiplexer_3_out, multiplexer_4_out;
  wire [3:0] opcode;
  wire [7:0] fromKeyBoard;
  wire [11:0] address, PC;
  wire [15:0] ALUout, fromMux, fromNextPC, immediate, multiplexer_7_out, multiplexer_8_out, mux0, mux1,
       Mux1_minus, Mux2_minus, ram_1_data, RegFileData, s, t;
  wire [15:12] addrOut;

  Clock u_clk (.out(clk));
  TTY #(.rows(13), .cols(80), .trigger("falling")) tty_1 (.data(s[6:0]), .clk(clk), .we(\output ), .clr(reset));
  Adder16Bit adder16bit_1 (.result(mux1), .B({addrOut, PC}), .A(16'h1));  // open: Cout, out_3, out_4, out_5, out_6
  Adder16Bit adder16bit_2 (.result(mux0), .B(mux1), .A(immediate));  // open: Cout, out_3, out_4, out_5, out_6
  sign_extender sign_extender_1 (.\input (address[5:0]), .\output (immediate));
  singleReg singlereg_1 (.Reset(reset), .Enable(1'b1), .\output ({addrOut, PC}), .clk(clk), .\input (fromNextPC));
  ROM #(.addrWidth(16), .dataWidth(16)) rom_1 (.addr({addrOut, PC}), .data({opcode, address}));  // open: sel
  Comparator #(.width(16)) comparator_1 (.a(s), .b(t), .gt(comparator_1_gt));  // open: eq, lt
  Multiplexer #(.width(16), .enable("false")) multiplexer_1 (
    .in0(mux1), .in1(mux0), .out(Mux1_minus), .sel(comparator_1_gt));
  Comparator #(.width(16)) comparator_2 (.a(s), .b({16{1'b0}}), .eq(comparator_2_eq));  // open: gt, lt
  Multiplexer #(.width(16), .enable("false")) multiplexer_2 (
    .in0(mux1), .in1(mux0), .out(Mux2_minus), .sel(comparator_2_eq));
  not not_1 (not_1_out, clk);
  Multiplexer #(.width(3), .enable("false")) multiplexer_3 (
    .in0(multiplexer_4_out), .in1(3'b111), .out(multiplexer_3_out), .sel(jal));
  Multiplexer #(.width(3), .enable("false")) multiplexer_4 (
    .in0(address[8:6]), .in1(address[5:3]), .out(multiplexer_4_out), .sel(Rdst));
  Multiplexer #(.select(4), .width(16), .enable("false")) multiplexer_5 (
    .in0(mux1), .in1(mux1), .in2(mux1), .in3(mux1), .in4(mux1), .in5(mux1), .in6(mux1), .in7(Mux1_minus),
    .in8(Mux2_minus), .in9(mux1), .in10(mux1), .in11({addrOut, address}), .in12(s),
    .in13({addrOut, address}), .in14(mux1), .in15(mux1), .out(fromNextPC), .sel(opcode));
  regfile regfile_1 (
    .D(RegFileData), .WE(WE), .clk(not_1_out), .rst(reset), .rs(address[11:9]), .rd(multiplexer_3_out),
    .rt(address[8:6]), .s(s), .t(t));
  Multiplexer #(.width(16), .enable("false")) multiplexer_6 (
    .in0(multiplexer_8_out), .in1(mux1), .out(RegFileData), .sel(jal));
  Controller controller_1 (
    .opcode(opcode), .rdst(Rdst), .Imm(Imm), .ALUop1(ALUbit1), .ALUop2(ALUbit2), .ALUop3(ALUbit3), .RWE(WE),
    .DMRE(DMRE), .DMWE(DMWE), .JAL(jal), .\output (\output ), .\input (\input ));
  Multiplexer #(.width(16), .enable("false")) multiplexer_7 (
    .in0(t), .in1(immediate), .out(multiplexer_7_out), .sel(Imm));
  Multiplexer #(.width(16), .enable("false")) multiplexer_8 (
    .in0(fromMux), .in1({{8{1'b0}}, fromKeyBoard}), .out(multiplexer_8_out), .sel(\input ));
  Keyboard keyboard_1 (.clk(clk), .re(\input ), .clr(reset), .avail(keyboard_1_avail), .data(fromKeyBoard[6:0]));
  ALU alu_1 (.Shift(address[2:0]), .s(s), .OpType({ALUbit3, ALUbit2, ALUbit1}), .t(multiplexer_7_out), .out(ALUout));
  not not_2 (fromKeyBoard[7], keyboard_1_avail);
  not not_3 (not_3_out, clk);
  RAM #(.addrWidth(16), .dataWidth(16), .bus("separate")) ram_1 (
    .addr(ALUout), .din(t), .data(ram_1_data), .str(DMWE), .clk(not_3_out));  // open: sel, ld, clr
  Multiplexer #(.width(16), .enable("false")) multiplexer_9 (.in0(ALUout), .in1(ram_1_data), .out(fromMux), .sel(DMRE));

  // Other names for the same wires on the sheet: addrOut[11:0] = address; shamt[2:0] = address[2:0];
  //   rd[2:0] = address[5:3]; rt[2:0] = address[8:6]; rs[2:0] = address[11:9]; PC[15:12] = addrOut; PC_1[15:0] = mux1

  // Notes on the sheet:
  //   NEXT PC
  //   PC holds register of current instruction
  //   TTY
  //   instruction memory
  //   split last 6 bits then put together through sx
  //   For addi type instructions, need sign extender
  //   contents of rom_1 (hex, n*v repeats v):
  //   20c0 204f 2090 7441 803f d009 8206 2441 803f 2271 ce00 2441 803f b00f 3488 803f
  //   bgt
  //   PC+1
  //   beqz
  //   no MIPS instruction writes >1, reads >2
  //   specifies reg7 as dest
  //   CONTROL
  //   Data Memory
endmodule

module regfile (
  input  [15:0] D,
  input  WE,
  input  [2:0] rs,
  input  clk,
  input  rst,
  input  [2:0] rd,
  input  [2:0] rt,
  output [15:0] s,
  output [15:0] t
);

  wire _1, _2, _3, _4, _5, _6, _7, and_1_out, and_2_out, and_3_out, and_4_out, and_5_out, and_6_out,
       and_7_out;
  wire [15:0] r0, r1, r2, r3, r4, r5, r6, r7;

  regDecoder regdecoder_1 (
    .rd(rd), .out1(_1), .out2(_2), .out3(_3), .out4(_4), .out5(_5), .out6(_6), .out7(_7));  // open: out0
  singleReg singlereg_1 (.Reset(rst), .Enable(1'b0), .\output (r0), .clk(clk), .\input (D));
  and and_1 (and_1_out, WE, _1);
  and and_2 (and_2_out, WE, _2);
  and and_3 (and_3_out, WE, _3);
  and and_4 (and_4_out, WE, _4);
  and and_5 (and_5_out, WE, _5);
  and and_6 (and_6_out, WE, _6);
  and and_7 (and_7_out, WE, _7);
  singleReg singlereg_2 (.Reset(rst), .Enable(and_1_out), .\output (r1), .clk(clk), .\input (D));
  singleReg singlereg_3 (.Reset(rst), .Enable(and_2_out), .\output (r2), .clk(clk), .\input (D));
  singleReg singlereg_4 (.Reset(rst), .Enable(and_3_out), .\output (r3), .clk(clk), .\input (D));
  singleReg singlereg_5 (.Reset(rst), .Enable(and_4_out), .\output (r4), .clk(clk), .\input (D));
  singleReg singlereg_6 (.Reset(rst), .Enable(and_5_out), .\output (r5), .clk(clk), .\input (D));
  singleReg singlereg_7 (.Reset(rst), .Enable(and_6_out), .\output (r6), .clk(clk), .\input (D));
  singleReg singlereg_8 (.Reset(rst), .Enable(and_7_out), .\output (r7), .clk(clk), .\input (D));
  // Probe on r0
  // Probe on r1
  // Probe on r2
  // Probe on r3
  Multiplexer #(.select(3), .width(16), .enable("false")) multiplexer_1 (
    .in0(r0), .in1(r1), .in2(r2), .in3(r3), .in4(r4), .in5(r5), .in6(r6), .in7(r7), .out(s), .sel(rs));
  Multiplexer #(.select(3), .width(16), .enable("false")) multiplexer_2 (
    .in0(r0), .in1(r1), .in2(r2), .in3(r3), .in4(r4), .in5(r5), .in6(r6), .in7(r7), .out(t), .sel(rt));
  // Probe on r4
  // Probe on r5
  // Probe on r6
  // Probe on r7

  // Notes on the sheet:
  //   DECODER: only 1 output not equal 0
endmodule

module ALU (
  input  [2:0] Shift,
  input  [2:0] OpType,
  input  [15:0] s,
  input  [15:0] t,
  output [15:0] out
);

  wire [15:0] add, ls, \nand , rs, sub, \xor ;

  shiftRight rightShift (.\input (s), .op(Shift), .\output (rs));
  Adder16Bit _16bitadder (.result(add), .B(t), .A(s));  // open: Cout, out_3, out_4, out_5, out_6
  shiftLeft leftShift (.\input (s), .bits(Shift), .\output (ls));
  subtractor u_sub (.A(s), .B(t), .\output (sub));  // open: COut
  assign \nand  = ~(s & t);  // NAND_Gate nand_1, 16 bits wide
  assign \xor  = s ^ t;  // XOR_Gate xor_1, 16 bits wide
  Multiplexer #(.select(3), .width(16), .enable("false")) multiplexer_1 (
    .in0(ls), .in1(rs), .in2(add), .in3(sub), .in4(\xor ), .in5(\nand ), .out(out), .sel(OpType));  // open: in6, in7
endmodule

module Controller (
  input  [3:0] opcode,
  output rdst,
  output Imm,
  output ALUop1,
  output ALUop2,
  output ALUop3,
  output RWE,
  output DMRE,
  output DMWE,
  output JAL,
  output \output ,
  output \input 
);

  wire add, addi, beqz, bgt, j, jr, \nand , not_1_out, not_2_out, not_3_out, not_4_out, not_5_out, not_6_out,
       not_7_out, not_8_out, not_9_out, not_10_out, not_11_out, not_12_out, not_13_out, not_14_out,
       not_15_out, not_16_out, not_17_out, not_18_out, not_19_out, not_20_out, not_21_out, not_22_out,
       not_23_out, not_24_out, not_25_out, not_26_out, not_27_out, not_28_out, not_29_out, not_30_out,
       not_31_out, not_32_out, shl, shra, sub, \xor ;

  not not_1 (not_1_out, opcode[3]);
  not not_2 (not_2_out, opcode[2]);
  not not_3 (not_3_out, opcode[1]);
  not not_4 (not_4_out, opcode[0]);
  not not_5 (not_5_out, opcode[3]);
  not not_6 (not_6_out, opcode[2]);
  not not_7 (not_7_out, opcode[1]);
  not not_8 (not_8_out, opcode[3]);
  not not_9 (not_9_out, opcode[2]);
  not not_10 (not_10_out, opcode[0]);
  not not_11 (not_11_out, opcode[3]);
  not not_12 (not_12_out, opcode[2]);
  not not_13 (not_13_out, opcode[3]);
  not not_14 (not_14_out, opcode[1]);
  not not_15 (not_15_out, opcode[0]);
  not not_16 (not_16_out, opcode[3]);
  not not_17 (not_17_out, opcode[1]);
  not not_18 (not_18_out, opcode[3]);
  not not_19 (not_19_out, opcode[0]);
  not not_20 (not_20_out, opcode[3]);
  not not_21 (not_21_out, opcode[2]);
  not not_22 (not_22_out, opcode[1]);
  not not_23 (not_23_out, opcode[0]);
  not not_24 (not_24_out, opcode[2]);
  not not_25 (not_25_out, opcode[1]);
  not not_26 (not_26_out, opcode[2]);
  not not_27 (not_27_out, opcode[0]);
  not not_28 (not_28_out, opcode[2]);
  not not_29 (not_29_out, opcode[1]);
  not not_30 (not_30_out, opcode[0]);
  not not_31 (not_31_out, opcode[1]);
  not not_32 (not_32_out, opcode[0]);
  and u_nand (\nand , not_1_out, not_2_out, not_3_out, not_4_out);
  and u_xor (\xor , not_5_out, not_6_out, not_7_out, opcode[0]);
  and u_addi (addi, not_8_out, not_9_out, opcode[1], not_10_out);
  and u_add (add, not_11_out, not_12_out, opcode[1], opcode[0]);
  and u_sub (sub, not_13_out, opcode[2], not_14_out, not_15_out);
  and u_shra (shra, not_16_out, opcode[2], not_17_out, opcode[0]);
  and u_shl (shl, not_18_out, opcode[2], opcode[1], not_19_out);
  and u_bgt (bgt, not_20_out, opcode[2], opcode[1], opcode[0]);
  and u_beqz (beqz, opcode[3], not_21_out, not_22_out, not_23_out);
  and lw (DMRE, opcode[3], not_24_out, not_25_out, opcode[0]);
  and sw (DMWE, opcode[3], not_26_out, opcode[1], not_27_out);
  and u_j (j, opcode[3], not_28_out, opcode[1], opcode[0]);
  and u_jr (jr, opcode[3], opcode[2], not_29_out, not_30_out);
  and u_jal (JAL, opcode[3], opcode[2], not_31_out, opcode[0]);
  and u_output (\output , opcode[3], opcode[2], opcode[1], not_32_out);
  and u_input (\input , opcode[3], opcode[2], opcode[1], opcode[0]);
  or or_1 (rdst, \nand , \xor , add, shl, shra, \input , sub);
  or or_2 (Imm, addi, beqz, DMRE, DMWE, bgt);
  or or_3 (ALUop1, \nand , sub, shra);
  or or_4 (ALUop2, add, addi, beqz, JAL, \output , \input , jr, j, JAL, beqz, bgt, DMWE, sub, DMRE);
  or or_5 (ALUop3, bgt, jr, j, \nand , \xor , \output , \input , beqz);
  or or_6 (RWE, \xor , add, shl, addi, JAL, sub, shra, DMRE, \nand , \input );

  // Other names for the same wires on the sheet: lw = DMRE; _0 = opcode[0]; _1 = opcode[1]; _2 = opcode[2];
  //   _3 = opcode[3]; sw = DMWE
endmodule

// sx
module sign_extender (
  input  [5:0] \input ,
  output [15:0] \output 
);


  assign \output  = {{11{\input [5]}}, \input [4:0]};

  // Other names for the same wires on the sheet: rest = \input [5]
endmodule

// register
module singleReg (
  input  clk,
  input  [15:0] \input ,
  input  Reset,
  input  Enable,
  output [15:0] \output 
);

  D_Flip_Flop d_ff_1 (.clk(clk), .D(\input [0]), .Q(\output [0]), .en(Enable), .reset(Reset));  // open: Qn, preset
  D_Flip_Flop d_ff_2 (.clk(clk), .D(\input [1]), .Q(\output [1]), .en(Enable), .reset(Reset));  // open: Qn, preset
  D_Flip_Flop d_ff_3 (.clk(clk), .D(\input [2]), .Q(\output [2]), .en(Enable), .reset(Reset));  // open: Qn, preset
  D_Flip_Flop d_ff_4 (.clk(clk), .D(\input [3]), .Q(\output [3]), .en(Enable), .reset(Reset));  // open: Qn, preset
  D_Flip_Flop d_ff_5 (.clk(clk), .D(\input [4]), .Q(\output [4]), .en(Enable), .reset(Reset));  // open: Qn, preset
  D_Flip_Flop d_ff_6 (.clk(clk), .D(\input [5]), .Q(\output [5]), .en(Enable), .reset(Reset));  // open: Qn, preset
  D_Flip_Flop d_ff_7 (.clk(clk), .D(\input [6]), .Q(\output [6]), .en(Enable), .reset(Reset));  // open: Qn, preset
  D_Flip_Flop d_ff_8 (.clk(clk), .D(\input [7]), .Q(\output [7]), .en(Enable), .reset(Reset));  // open: Qn, preset
  D_Flip_Flop d_ff_9 (.clk(clk), .D(\input [8]), .Q(\output [8]), .en(Enable), .reset(Reset));  // open: Qn, preset
  D_Flip_Flop d_ff_10 (.clk(clk), .D(\input [9]), .Q(\output [9]), .en(Enable), .reset(Reset));  // open: Qn, preset
  D_Flip_Flop d_ff_11 (.clk(clk), .D(\input [10]), .Q(\output [10]), .en(Enable), .reset(Reset));  // open: Qn, preset
  D_Flip_Flop d_ff_12 (.clk(clk), .D(\input [11]), .Q(\output [11]), .en(Enable), .reset(Reset));  // open: Qn, preset
  D_Flip_Flop d_ff_13 (.clk(clk), .D(\input [12]), .Q(\output [12]), .en(Enable), .reset(Reset));  // open: Qn, preset
  D_Flip_Flop d_ff_14 (.clk(clk), .D(\input [13]), .Q(\output [13]), .en(Enable), .reset(Reset));  // open: Qn, preset
  D_Flip_Flop d_ff_15 (.clk(clk), .D(\input [14]), .Q(\output [14]), .en(Enable), .reset(Reset));  // open: Qn, preset
  D_Flip_Flop d_ff_16 (.clk(clk), .D(\input [15]), .Q(\output [15]), .en(Enable), .reset(Reset));  // open: Qn, preset

  // Other names for the same wires on the sheet: in0 = \input [0]; in1 = \input [1]; in2 = \input [2];
  //   in3 = \input [3]; in4 = \input [4]; in5 = \input [5]; in6 = \input [6]; in7 = \input [7]; in8 = \input [8];
  //   in9 = \input [9]; in10 = \input [10]; in11 = \input [11]; in12 = \input [12]; in13 = \input [13];
  //   in14 = \input [14]; in15 = \input [15]; _0 = \output [0]; _1 = \output [1]; _2 = \output [2]; _3 = \output [3];
  //   _4 = \output [4]; _5 = \output [5]; _6 = \output [6]; _7 = \output [7]; _8 = \output [8]; _9 = \output [9];
  //   _10 = \output [10]; _11 = \output [11]; _12 = \output [12]; _13 = \output [13]; _14 = \output [14];
  //   _15 = \output [15]
endmodule

// DECODER
module regDecoder (
  input  [2:0] rd,
  output out0,
  output out1,
  output out2,
  output out3,
  output out4,
  output out5,
  output out6,
  output out7
);

  wire not_1_out, not_2_out, not_3_out, not_4_out, not_5_out, not_6_out, not_7_out, not_8_out, not_9_out,
       not_10_out, not_11_out, not_12_out;

  not not_1 (not_1_out, rd[0]);
  not not_2 (not_2_out, rd[1]);
  not not_3 (not_3_out, rd[2]);
  not not_4 (not_4_out, rd[1]);
  not not_5 (not_5_out, rd[2]);
  not not_6 (not_6_out, rd[0]);
  not not_7 (not_7_out, rd[2]);
  not not_8 (not_8_out, rd[2]);
  not not_9 (not_9_out, rd[0]);
  not not_10 (not_10_out, rd[1]);
  not not_11 (not_11_out, rd[1]);
  not not_12 (not_12_out, rd[0]);
  and and_1 (out0, not_1_out, not_2_out, not_3_out);
  and and_2 (out1, rd[0], not_4_out, not_5_out);
  and and_3 (out2, not_6_out, rd[1], not_7_out);
  and and_4 (out3, rd[0], rd[1], not_8_out);
  and and_5 (out4, not_9_out, not_10_out, rd[2]);
  and and_6 (out5, rd[0], not_11_out, rd[2]);
  and and_7 (out6, not_12_out, rd[1], rd[2]);
  and and_8 (out7, rd[0], rd[1], rd[2]);

  // Other names for the same wires on the sheet: bit1 = rd[0]; bit2 = rd[1]; bit3 = rd[2]

  // Notes on the sheet:
  //   R1: 000
  //   001
  //   010
  //   011
  //   100
  //   101
  //   110
  //   111
endmodule

module shiftLeft (
  input  [15:0] \input ,
  input  [2:0] bits,
  output [15:0] \output 
);

  wire multiplexer_1_out, multiplexer_2_out, multiplexer_3_out, multiplexer_4_out, multiplexer_5_out,
       multiplexer_6_out, multiplexer_7_out, multiplexer_8_out, multiplexer_9_out, multiplexer_10_out,
       multiplexer_11_out, multiplexer_12_out, multiplexer_13_out, multiplexer_14_out, multiplexer_15_out,
       multiplexer_16_out, multiplexer_17_out, multiplexer_18_out, multiplexer_19_out, multiplexer_20_out,
       multiplexer_21_out, multiplexer_22_out, multiplexer_23_out, multiplexer_24_out, multiplexer_25_out,
       multiplexer_26_out, multiplexer_27_out, multiplexer_28_out, multiplexer_29_out, multiplexer_30_out,
       multiplexer_31_out, multiplexer_32_out;

  Multiplexer #(.enable("false")) multiplexer_1 (.in0(\input [0]), .in1(1'b0), .out(multiplexer_1_out), .sel(bits[0]));
  Multiplexer #(.enable("false")) multiplexer_2 (
    .in0(\input [1]), .in1(\input [0]), .out(multiplexer_2_out), .sel(bits[0]));
  Multiplexer #(.enable("false")) multiplexer_3 (
    .in0(\input [2]), .in1(\input [1]), .out(multiplexer_3_out), .sel(bits[0]));
  Multiplexer #(.enable("false")) multiplexer_4 (
    .in0(\input [3]), .in1(\input [2]), .out(multiplexer_4_out), .sel(bits[0]));
  Multiplexer #(.enable("false")) multiplexer_5 (
    .in0(\input [4]), .in1(\input [3]), .out(multiplexer_5_out), .sel(bits[0]));
  Multiplexer #(.enable("false")) multiplexer_6 (
    .in0(\input [5]), .in1(\input [4]), .out(multiplexer_6_out), .sel(bits[0]));
  Multiplexer #(.enable("false")) multiplexer_7 (
    .in0(\input [6]), .in1(\input [5]), .out(multiplexer_7_out), .sel(bits[0]));
  Multiplexer #(.enable("false")) multiplexer_8 (
    .in0(\input [7]), .in1(\input [6]), .out(multiplexer_8_out), .sel(bits[0]));
  Multiplexer #(.enable("false")) multiplexer_9 (
    .in0(\input [8]), .in1(\input [7]), .out(multiplexer_9_out), .sel(bits[0]));
  Multiplexer #(.enable("false")) multiplexer_10 (
    .in0(\input [9]), .in1(\input [8]), .out(multiplexer_10_out), .sel(bits[0]));
  Multiplexer #(.enable("false")) multiplexer_11 (
    .in0(\input [10]), .in1(\input [9]), .out(multiplexer_11_out), .sel(bits[0]));
  Multiplexer #(.enable("false")) multiplexer_12 (
    .in0(\input [11]), .in1(\input [10]), .out(multiplexer_12_out), .sel(bits[0]));
  Multiplexer #(.enable("false")) multiplexer_13 (
    .in0(\input [12]), .in1(\input [11]), .out(multiplexer_13_out), .sel(bits[0]));
  Multiplexer #(.enable("false")) multiplexer_14 (
    .in0(\input [13]), .in1(\input [12]), .out(multiplexer_14_out), .sel(bits[0]));
  Multiplexer #(.enable("false")) multiplexer_15 (
    .in0(\input [14]), .in1(\input [13]), .out(multiplexer_15_out), .sel(bits[0]));
  Multiplexer #(.enable("false")) multiplexer_16 (
    .in0(\input [15]), .in1(\input [14]), .out(multiplexer_16_out), .sel(bits[0]));
  Multiplexer #(.enable("false")) multiplexer_17 (
    .in0(multiplexer_1_out), .in1(1'b0), .out(multiplexer_17_out), .sel(bits[1]));
  Multiplexer #(.enable("false")) multiplexer_18 (
    .in0(multiplexer_2_out), .in1(1'b0), .out(multiplexer_18_out), .sel(bits[1]));
  Multiplexer #(.enable("false")) multiplexer_19 (
    .in0(multiplexer_3_out), .in1(multiplexer_1_out), .out(multiplexer_19_out), .sel(bits[1]));
  Multiplexer #(.enable("false")) multiplexer_20 (
    .in0(multiplexer_4_out), .in1(multiplexer_2_out), .out(multiplexer_20_out), .sel(bits[1]));
  Multiplexer #(.enable("false")) multiplexer_21 (
    .in0(multiplexer_5_out), .in1(multiplexer_3_out), .out(multiplexer_21_out), .sel(bits[1]));
  Multiplexer #(.enable("false")) multiplexer_22 (
    .in0(multiplexer_6_out), .in1(multiplexer_4_out), .out(multiplexer_22_out), .sel(bits[1]));
  Multiplexer #(.enable("false")) multiplexer_23 (
    .in0(multiplexer_7_out), .in1(multiplexer_5_out), .out(multiplexer_23_out), .sel(bits[1]));
  Multiplexer #(.enable("false")) multiplexer_24 (
    .in0(multiplexer_8_out), .in1(multiplexer_6_out), .out(multiplexer_24_out), .sel(bits[1]));
  Multiplexer #(.enable("false")) multiplexer_25 (
    .in0(multiplexer_9_out), .in1(multiplexer_7_out), .out(multiplexer_25_out), .sel(bits[1]));
  Multiplexer #(.enable("false")) multiplexer_26 (
    .in0(multiplexer_10_out), .in1(multiplexer_8_out), .out(multiplexer_26_out), .sel(bits[1]));
  Multiplexer #(.enable("false")) multiplexer_27 (
    .in0(multiplexer_11_out), .in1(multiplexer_9_out), .out(multiplexer_27_out), .sel(bits[1]));
  Multiplexer #(.enable("false")) multiplexer_28 (
    .in0(multiplexer_12_out), .in1(multiplexer_10_out), .out(multiplexer_28_out), .sel(bits[1]));
  Multiplexer #(.enable("false")) multiplexer_29 (
    .in0(multiplexer_13_out), .in1(multiplexer_11_out), .out(multiplexer_29_out), .sel(bits[1]));
  Multiplexer #(.enable("false")) multiplexer_30 (
    .in0(multiplexer_14_out), .in1(multiplexer_12_out), .out(multiplexer_30_out), .sel(bits[1]));
  Multiplexer #(.enable("false")) multiplexer_31 (
    .in0(multiplexer_15_out), .in1(multiplexer_13_out), .out(multiplexer_31_out), .sel(bits[1]));
  Multiplexer #(.enable("false")) multiplexer_32 (
    .in0(multiplexer_16_out), .in1(multiplexer_14_out), .out(multiplexer_32_out), .sel(bits[1]));
  Multiplexer #(.enable("false")) multiplexer_33 (
    .in0(multiplexer_17_out), .in1(1'b0), .out(\output [0]), .sel(bits[2]));
  Multiplexer #(.enable("false")) multiplexer_34 (
    .in0(multiplexer_18_out), .in1(1'b0), .out(\output [1]), .sel(bits[2]));
  Multiplexer #(.enable("false")) multiplexer_35 (
    .in0(multiplexer_19_out), .in1(1'b0), .out(\output [2]), .sel(bits[2]));
  Multiplexer #(.enable("false")) multiplexer_36 (
    .in0(multiplexer_20_out), .in1(1'b0), .out(\output [3]), .sel(bits[2]));
  Multiplexer #(.enable("false")) multiplexer_37 (
    .in0(multiplexer_21_out), .in1(multiplexer_17_out), .out(\output [4]), .sel(bits[2]));
  Multiplexer #(.enable("false")) multiplexer_38 (
    .in0(multiplexer_22_out), .in1(multiplexer_18_out), .out(\output [5]), .sel(bits[2]));
  Multiplexer #(.enable("false")) multiplexer_39 (
    .in0(multiplexer_23_out), .in1(multiplexer_19_out), .out(\output [6]), .sel(bits[2]));
  Multiplexer #(.enable("false")) multiplexer_40 (
    .in0(multiplexer_24_out), .in1(multiplexer_20_out), .out(\output [7]), .sel(bits[2]));
  Multiplexer #(.enable("false")) multiplexer_41 (
    .in0(multiplexer_25_out), .in1(multiplexer_21_out), .out(\output [8]), .sel(bits[2]));
  Multiplexer #(.enable("false")) multiplexer_42 (
    .in0(multiplexer_26_out), .in1(multiplexer_22_out), .out(\output [9]), .sel(bits[2]));
  Multiplexer #(.enable("false")) multiplexer_43 (
    .in0(multiplexer_27_out), .in1(multiplexer_23_out), .out(\output [10]), .sel(bits[2]));
  Multiplexer #(.enable("false")) multiplexer_44 (
    .in0(multiplexer_28_out), .in1(multiplexer_24_out), .out(\output [11]), .sel(bits[2]));
  Multiplexer #(.enable("false")) multiplexer_45 (
    .in0(multiplexer_29_out), .in1(multiplexer_25_out), .out(\output [12]), .sel(bits[2]));
  Multiplexer #(.enable("false")) multiplexer_46 (
    .in0(multiplexer_30_out), .in1(multiplexer_26_out), .out(\output [13]), .sel(bits[2]));
  Multiplexer #(.enable("false")) multiplexer_47 (
    .in0(multiplexer_31_out), .in1(multiplexer_27_out), .out(\output [14]), .sel(bits[2]));
  Multiplexer #(.enable("false")) multiplexer_48 (
    .in0(multiplexer_32_out), .in1(multiplexer_28_out), .out(\output [15]), .sel(bits[2]));

  // Other names for the same wires on the sheet: bit0 = bits[0]; bit1 = bits[1]; bit2 = bits[2]; _0 = \input [0];
  //   _1 = \input [1]; _2 = \input [2]; _3 = \input [3]; _4 = \input [4]; _5 = \input [5]; _6 = \input [6];
  //   _7 = \input [7]; _8 = \input [8]; _9 = \input [9]; _10 = \input [10]; _11 = \input [11]; _12 = \input [12];
  //   _13 = \input [13]; _14 = \input [14]; _15 = \input [15]; out1 = \output [0]; out2 = \output [1];
  //   out3 = \output [2]; out4 = \output [3]; out5 = \output [4]; out6 = \output [5]; out7 = \output [6];
  //   out8 = \output [7]; out9 = \output [8]; out10 = \output [9]; out11 = \output [10]; out12 = \output [11];
  //   out13 = \output [12]; out14 = \output [13]; out15 = \output [14]; out16 = \output [15]
endmodule

module shiftRight (
  input  [15:0] \input ,
  input  [2:0] op,
  output [15:0] \output 
);

  wire multiplexer_1_out, multiplexer_2_out, multiplexer_3_out, multiplexer_4_out, multiplexer_5_out,
       multiplexer_6_out, multiplexer_7_out, multiplexer_8_out, multiplexer_9_out, multiplexer_10_out,
       multiplexer_11_out, multiplexer_12_out, multiplexer_13_out, multiplexer_14_out, multiplexer_15_out,
       multiplexer_16_out, multiplexer_17_out, multiplexer_18_out, multiplexer_19_out, multiplexer_20_out,
       multiplexer_21_out, multiplexer_22_out, multiplexer_23_out, multiplexer_24_out, multiplexer_25_out,
       multiplexer_26_out, multiplexer_27_out, multiplexer_28_out, multiplexer_29_out, multiplexer_30_out,
       multiplexer_31_out, multiplexer_32_out;

  Multiplexer #(.enable("false")) multiplexer_1 (
    .in0(\input [0]), .in1(\input [1]), .out(multiplexer_1_out), .sel(op[0]));
  Multiplexer #(.enable("false")) multiplexer_2 (
    .in0(\input [1]), .in1(\input [2]), .out(multiplexer_2_out), .sel(op[0]));
  Multiplexer #(.enable("false")) multiplexer_3 (
    .in0(\input [2]), .in1(\input [3]), .out(multiplexer_3_out), .sel(op[0]));
  Multiplexer #(.enable("false")) multiplexer_4 (
    .in0(\input [3]), .in1(\input [4]), .out(multiplexer_4_out), .sel(op[0]));
  Multiplexer #(.enable("false")) multiplexer_5 (
    .in0(\input [4]), .in1(\input [5]), .out(multiplexer_5_out), .sel(op[0]));
  Multiplexer #(.enable("false")) multiplexer_6 (
    .in0(\input [5]), .in1(\input [6]), .out(multiplexer_6_out), .sel(op[0]));
  Multiplexer #(.enable("false")) multiplexer_7 (
    .in0(\input [6]), .in1(\input [7]), .out(multiplexer_7_out), .sel(op[0]));
  Multiplexer #(.enable("false")) multiplexer_8 (
    .in0(\input [7]), .in1(\input [8]), .out(multiplexer_8_out), .sel(op[0]));
  Multiplexer #(.enable("false")) multiplexer_9 (
    .in0(\input [8]), .in1(\input [9]), .out(multiplexer_9_out), .sel(op[0]));
  Multiplexer #(.enable("false")) multiplexer_10 (
    .in0(\input [9]), .in1(\input [10]), .out(multiplexer_10_out), .sel(op[0]));
  Multiplexer #(.enable("false")) multiplexer_11 (
    .in0(\input [10]), .in1(\input [11]), .out(multiplexer_11_out), .sel(op[0]));
  Multiplexer #(.enable("false")) multiplexer_12 (
    .in0(\input [11]), .in1(\input [12]), .out(multiplexer_12_out), .sel(op[0]));
  Multiplexer #(.enable("false")) multiplexer_13 (
    .in0(\input [12]), .in1(\input [13]), .out(multiplexer_13_out), .sel(op[0]));
  Multiplexer #(.enable("false")) multiplexer_14 (
    .in0(\input [13]), .in1(\input [14]), .out(multiplexer_14_out), .sel(op[0]));
  Multiplexer #(.enable("false")) multiplexer_15 (
    .in0(\input [14]), .in1(\input [15]), .out(multiplexer_15_out), .sel(op[0]));
  Multiplexer #(.enable("false")) multiplexer_16 (
    .in0(\input [15]), .in1(\input [15]), .out(multiplexer_16_out), .sel(op[0]));
  Multiplexer #(.enable("false")) multiplexer_17 (
    .in0(multiplexer_1_out), .in1(multiplexer_3_out), .out(multiplexer_17_out), .sel(op[1]));
  Multiplexer #(.enable("false")) multiplexer_18 (
    .in0(multiplexer_2_out), .in1(multiplexer_4_out), .out(multiplexer_18_out), .sel(op[1]));
  Multiplexer #(.enable("false")) multiplexer_19 (
    .in0(multiplexer_3_out), .in1(multiplexer_5_out), .out(multiplexer_19_out), .sel(op[1]));
  Multiplexer #(.enable("false")) multiplexer_20 (
    .in0(multiplexer_4_out), .in1(multiplexer_6_out), .out(multiplexer_20_out), .sel(op[1]));
  Multiplexer #(.enable("false")) multiplexer_21 (
    .in0(multiplexer_5_out), .in1(multiplexer_7_out), .out(multiplexer_21_out), .sel(op[1]));
  Multiplexer #(.enable("false")) multiplexer_22 (
    .in0(multiplexer_6_out), .in1(multiplexer_8_out), .out(multiplexer_22_out), .sel(op[1]));
  Multiplexer #(.enable("false")) multiplexer_23 (
    .in0(multiplexer_7_out), .in1(multiplexer_9_out), .out(multiplexer_23_out), .sel(op[1]));
  Multiplexer #(.enable("false")) multiplexer_24 (
    .in0(multiplexer_8_out), .in1(multiplexer_10_out), .out(multiplexer_24_out), .sel(op[1]));
  Multiplexer #(.enable("false")) multiplexer_25 (
    .in0(multiplexer_9_out), .in1(multiplexer_11_out), .out(multiplexer_25_out), .sel(op[1]));
  Multiplexer #(.enable("false")) multiplexer_26 (
    .in0(multiplexer_10_out), .in1(multiplexer_12_out), .out(multiplexer_26_out), .sel(op[1]));
  Multiplexer #(.enable("false")) multiplexer_27 (
    .in0(multiplexer_11_out), .in1(multiplexer_13_out), .out(multiplexer_27_out), .sel(op[1]));
  Multiplexer #(.enable("false")) multiplexer_28 (
    .in0(multiplexer_12_out), .in1(multiplexer_14_out), .out(multiplexer_28_out), .sel(op[1]));
  Multiplexer #(.enable("false")) multiplexer_29 (
    .in0(multiplexer_13_out), .in1(multiplexer_15_out), .out(multiplexer_29_out), .sel(op[1]));
  Multiplexer #(.enable("false")) multiplexer_30 (
    .in0(multiplexer_14_out), .in1(multiplexer_16_out), .out(multiplexer_30_out), .sel(op[1]));
  Multiplexer #(.enable("false")) multiplexer_31 (
    .in0(multiplexer_15_out), .in1(\input [15]), .out(multiplexer_31_out), .sel(op[1]));
  Multiplexer #(.enable("false")) multiplexer_32 (
    .in0(multiplexer_16_out), .in1(\input [15]), .out(multiplexer_32_out), .sel(op[1]));
  Multiplexer #(.enable("false")) multiplexer_33 (
    .in0(multiplexer_17_out), .in1(multiplexer_21_out), .out(\output [0]), .sel(op[2]));
  Multiplexer #(.enable("false")) multiplexer_34 (
    .in0(multiplexer_18_out), .in1(multiplexer_22_out), .out(\output [1]), .sel(op[2]));
  Multiplexer #(.enable("false")) multiplexer_35 (
    .in0(multiplexer_19_out), .in1(multiplexer_23_out), .out(\output [2]), .sel(op[2]));
  Multiplexer #(.enable("false")) multiplexer_36 (
    .in0(multiplexer_20_out), .in1(multiplexer_24_out), .out(\output [3]), .sel(op[2]));
  Multiplexer #(.enable("false")) multiplexer_37 (
    .in0(multiplexer_21_out), .in1(multiplexer_25_out), .out(\output [4]), .sel(op[2]));
  Multiplexer #(.enable("false")) multiplexer_38 (
    .in0(multiplexer_22_out), .in1(multiplexer_26_out), .out(\output [5]), .sel(op[2]));
  Multiplexer #(.enable("false")) multiplexer_39 (
    .in0(multiplexer_23_out), .in1(multiplexer_27_out), .out(\output [6]), .sel(op[2]));
  Multiplexer #(.enable("false")) multiplexer_40 (
    .in0(multiplexer_24_out), .in1(multiplexer_28_out), .out(\output [7]), .sel(op[2]));
  Multiplexer #(.enable("false")) multiplexer_41 (
    .in0(multiplexer_25_out), .in1(multiplexer_29_out), .out(\output [8]), .sel(op[2]));
  Multiplexer #(.enable("false")) multiplexer_42 (
    .in0(multiplexer_26_out), .in1(multiplexer_30_out), .out(\output [9]), .sel(op[2]));
  Multiplexer #(.enable("false")) multiplexer_43 (
    .in0(multiplexer_27_out), .in1(multiplexer_31_out), .out(\output [10]), .sel(op[2]));
  Multiplexer #(.enable("false")) multiplexer_44 (
    .in0(multiplexer_28_out), .in1(multiplexer_32_out), .out(\output [11]), .sel(op[2]));
  Multiplexer #(.enable("false")) multiplexer_45 (
    .in0(multiplexer_29_out), .in1(\input [15]), .out(\output [12]), .sel(op[2]));
  Multiplexer #(.enable("false")) multiplexer_46 (
    .in0(multiplexer_30_out), .in1(\input [15]), .out(\output [13]), .sel(op[2]));
  Multiplexer #(.enable("false")) multiplexer_47 (
    .in0(multiplexer_31_out), .in1(\input [15]), .out(\output [14]), .sel(op[2]));
  Multiplexer #(.enable("false")) multiplexer_48 (
    .in0(multiplexer_32_out), .in1(\input [15]), .out(\output [15]), .sel(op[2]));

  // Other names for the same wires on the sheet: in0 = \input [0]; in1 = \input [1]; in2 = \input [2];
  //   in3 = \input [3]; in4 = \input [4]; in5 = \input [5]; in6 = \input [6]; in7 = \input [7]; in8 = \input [8];
  //   in9 = \input [9]; in10 = \input [10]; in11 = \input [11]; in12 = \input [12]; in13 = \input [13];
  //   in14 = \input [14]; in15 = \input [15]; _0 = op[0]; _1 = op[1]; _2 = op[2]; out1 = \output [0];
  //   out2 = \output [1]; out3 = \output [2]; out4 = \output [3]; out5 = \output [4]; out6 = \output [5];
  //   out7 = \output [6]; out8 = \output [7]; out9 = \output [8]; out10 = \output [9]; out11 = \output [10];
  //   out12 = \output [11]; out13 = \output [12]; out14 = \output [13]; out15 = \output [14]; out16 = \output [15]
endmodule

module subtractor (
  input  [15:0] A,
  input  [15:0] B,
  output [15:0] \output ,
  output COut
);

  wire adder_1_cout, adder_2_cout, adder_3_cout, adder_4_cout, adder_5_cout, adder_6_cout, adder_7_cout,
       adder_8_cout, adder_9_cout, adder_10_cout, adder_11_cout, adder_12_cout, adder_13_cout, adder_14_cout,
       adder_15_cout, xor_1_out, xor_2_out, xor_3_out, xor_4_out, xor_5_out, xor_6_out, xor_7_out, xor_8_out,
       xor_9_out, xor_10_out, xor_11_out, xor_12_out, xor_13_out, xor_14_out, xor_15_out, xor_16_out;

  xor xor_1 (xor_1_out, 1'b1, B[0]);
  xor xor_2 (xor_2_out, 1'b1, B[1]);
  xor xor_3 (xor_3_out, 1'b1, B[2]);
  xor xor_4 (xor_4_out, 1'b1, B[3]);
  xor xor_5 (xor_5_out, 1'b1, B[4]);
  xor xor_6 (xor_6_out, 1'b1, B[5]);
  xor xor_7 (xor_7_out, 1'b1, B[6]);
  xor xor_8 (xor_8_out, 1'b1, B[7]);
  xor xor_9 (xor_9_out, 1'b1, B[8]);
  xor xor_10 (xor_10_out, 1'b1, B[9]);
  xor xor_11 (xor_11_out, 1'b1, B[10]);
  xor xor_12 (xor_12_out, 1'b1, B[11]);
  xor xor_13 (xor_13_out, 1'b1, B[12]);
  xor xor_14 (xor_14_out, 1'b1, B[13]);
  xor xor_15 (xor_15_out, 1'b1, B[14]);
  xor xor_16 (xor_16_out, 1'b1, B[15]);
  adder adder_1 (.A(A[0]), .B(xor_1_out), .CIn(1'b1), .COut(adder_1_cout), .Sum(\output [0]));
  adder adder_2 (.A(A[1]), .B(xor_2_out), .CIn(adder_1_cout), .COut(adder_2_cout), .Sum(\output [1]));
  adder adder_3 (.A(A[2]), .B(xor_3_out), .CIn(adder_2_cout), .COut(adder_3_cout), .Sum(\output [2]));
  adder adder_4 (.A(A[3]), .B(xor_4_out), .CIn(adder_3_cout), .COut(adder_4_cout), .Sum(\output [3]));
  adder adder_5 (.A(A[4]), .B(xor_5_out), .CIn(adder_4_cout), .COut(adder_5_cout), .Sum(\output [4]));
  adder adder_6 (.A(A[5]), .B(xor_6_out), .CIn(adder_5_cout), .COut(adder_6_cout), .Sum(\output [5]));
  adder adder_7 (.A(A[6]), .B(xor_7_out), .CIn(adder_6_cout), .COut(adder_7_cout), .Sum(\output [6]));
  adder adder_8 (.A(A[7]), .B(xor_8_out), .CIn(adder_7_cout), .COut(adder_8_cout), .Sum(\output [7]));
  adder adder_9 (.A(A[8]), .B(xor_9_out), .CIn(adder_8_cout), .COut(adder_9_cout), .Sum(\output [8]));
  adder adder_10 (.A(A[9]), .B(xor_10_out), .CIn(adder_9_cout), .COut(adder_10_cout), .Sum(\output [9]));
  adder adder_11 (.A(A[10]), .B(xor_11_out), .CIn(adder_10_cout), .COut(adder_11_cout), .Sum(\output [10]));
  adder adder_12 (.A(A[11]), .B(xor_12_out), .CIn(adder_11_cout), .COut(adder_12_cout), .Sum(\output [11]));
  adder adder_13 (.A(A[12]), .B(xor_13_out), .CIn(adder_12_cout), .COut(adder_13_cout), .Sum(\output [12]));
  adder adder_14 (.A(A[13]), .B(xor_14_out), .CIn(adder_13_cout), .COut(adder_14_cout), .Sum(\output [13]));
  adder adder_15 (.A(A[14]), .B(xor_15_out), .CIn(adder_14_cout), .COut(adder_15_cout), .Sum(\output [14]));
  adder adder_16 (.A(A[15]), .B(xor_16_out), .CIn(adder_15_cout), .COut(COut), .Sum(\output [15]));

  // Other names for the same wires on the sheet: out1 = \output [0]; out2 = \output [1]; out3 = \output [2];
  //   out4 = \output [3]; out5 = \output [4]; out6 = \output [5]; out7 = \output [6]; out8 = \output [7];
  //   out9 = \output [8]; out10 = \output [9]; out11 = \output [10]; out12 = \output [11]; out13 = \output [12];
  //   out14 = \output [13]; out15 = \output [14]; out16 = \output [15]
endmodule

module adder (
  input  CIn,
  input  A,
  input  B,
  output Sum,
  output COut
);

  wire and_1_out, and_2_out, xor_1_out;

  and and_1 (and_1_out, B, A);
  or or_1 (COut, and_1_out, and_2_out);
  xor xor_1 (xor_1_out, A, B);
  and and_2 (and_2_out, xor_1_out, CIn);
  xor xor_2 (Sum, CIn, xor_1_out);
endmodule

// 4Adder
module Adder4Bit (
  input  [3:0] A,
  input  carryin,
  input  [3:0] B,
  output carryout,
  output overflow,
  output [3:0] result
);

  wire adder_3_cout, adder_4_cout, cout1;

  adder adder_1 (.A(A[3]), .B(B[3]), .CIn(cout1), .COut(carryout), .Sum(result[3]));
  xor xor_1 (overflow, carryout, cout1);
  adder adder_2 (.A(A[2]), .B(B[2]), .CIn(adder_3_cout), .COut(cout1), .Sum(result[2]));
  adder adder_3 (.A(A[1]), .B(B[1]), .CIn(adder_4_cout), .COut(adder_3_cout), .Sum(result[1]));
  adder adder_4 (.A(A[0]), .B(B[0]), .CIn(carryin), .COut(adder_4_cout), .Sum(result[0]));

  // Other names for the same wires on the sheet: cout = carryout; _1 = result[0]; _2 = result[1]; _3 = result[2];
  //   _4 = result[3]
endmodule

// adder
module Adder16Bit (
  input  [15:0] B,
  input  [15:0] A,
  output out_3,
  output out_4,
  output out_5,
  output out_6,
  output Cout,
  output [15:0] result
);

  wire adder4bit_2_carryout, adder4bit_3_carryout, adder4bit_4_carryout;

  Adder4Bit adder4bit_1 (
    .A(A[15:12]), .carryout(Cout), .B(B[15:12]), .result(result[15:12]), .carryin(adder4bit_2_carryout),
    .overflow(out_3));
  Adder4Bit adder4bit_2 (
    .A(A[11:8]), .carryout(adder4bit_2_carryout), .B(B[11:8]), .result(result[11:8]),
    .carryin(adder4bit_3_carryout), .overflow(out_4));
  Adder4Bit adder4bit_3 (
    .A(A[7:4]), .carryout(adder4bit_3_carryout), .B(B[7:4]), .result(result[7:4]),
    .carryin(adder4bit_4_carryout), .overflow(out_5));
  Adder4Bit adder4bit_4 (
    .A(A[3:0]), .carryout(adder4bit_4_carryout), .B(B[3:0]), .result(result[3:0]), .carryin(1'b0),
    .overflow(out_6));

  // Other names for the same wires on the sheet: A0[3:0] = A[3:0]; A1[3:0] = A[7:4]; A2[3:0] = A[11:8];
  //   A3[3:0] = A[15:12]; B0[3:0] = B[3:0]; B1[3:0] = B[7:4]; B2[3:0] = B[11:8]; B3[3:0] = B[15:12];
  //   R0[3:0] = result[3:0]; R1[3:0] = result[7:4]; R2[3:0] = result[11:8]; R3[3:0] = result[15:12]
endmodule
