// Logisim project Task2.circ as structural Verilog: 1 circuit, main circuit main
module main (
  input  in1,
  input  in2,
  input  in3,
  output out_4
);

  wire and_1_out, and_2_out, and_3_out, and_4_out, not_1_out, not_2_out, not_3_out;

  not not_1 (not_1_out, in1);
  buf and_1 (and_1_out, in1);  // AND_Gate
  not not_2 (not_2_out, in1);
  and and_2 (and_2_out, not_1_out, in1, in1);
  not not_3 (not_3_out, in1);
  and and_3 (and_3_out, not_2_out, in1);
  buf and_4 (and_4_out, not_3_out);  // AND_Gate
  or or_1 (out_4, and_4_out, and_1_out, and_3_out, and_2_out);

  assign in2 = in1;
  assign in3 = in1;

  // Notes on the sheet:
  //   Recitation 6, Task 2
  //   1&2&3
  //   1&!2&!3
  //   !1&2&3
  //   !1&!2&!3
endmodule
