// Logisim project Task3.circ as structural Verilog: 3 circuits, main circuit main
module main (
  input  A,
  output out
);

  wire clock_1_out, D0_q, D1_out, D2_out, D_D1_q;

  D1 D1 (.A(A), .Q1(D_D1_q), .Q0(D0_q), .out(D1_out));
  D0 D2 (.A(A), .Q1(D_D1_q), .Q0(D0_q), .out(D2_out));
  Clock clock_1 (.out(clock_1_out));
  D_Flip_Flop D_D1 (.clk(clock_1_out), .D(D1_out), .Q(D_D1_q));  // open: Qn, preset, en, reset
  D_Flip_Flop D0 (.clk(clock_1_out), .D(D2_out), .Q(D0_q));  // open: Qn, preset, en, reset
  and Q1__Q0 (out, D_D1_q, D0_q);
endmodule

module D1 (
  input  A,
  input  Q1,
  input  Q0,
  output out
);

  wire Q1_Q0_out;

  or Q1_Q0 (Q1_Q0_out, Q1, Q0);
  and A__Q1_Q0 (out, A, Q1_Q0_out);
endmodule

module D0 (
  input  A,
  input  Q1,
  input  Q0,
  output out
);

  wire bothOR_out, not_1_out, Q1_nQ0_out, Q1_xnor_Q0_out;

  xor Q1_xnor_Q0 (Q1_xnor_Q0_out, Q1, Q0);
  and Q1_nQ0 (Q1_nQ0_out, Q1, not_1_out);
  not not_1 (not_1_out, Q0);
  or bothOR (bothOR_out, Q1_xnor_Q0_out, Q1_nQ0_out);
  and A_bothOR (out, A, bothOR_out);
endmodule
