// Logisim project Task4.circ as structural Verilog: 1 circuit, main circuit main
module main (
  input  in2,
  input  in3,
  output out_3
);

  wire and_1_out, and_2_out, not_1_out;

  not not_1 (not_1_out, in2);
  buf and_1 (and_1_out, in2);  // AND_Gate
  buf and_2 (and_2_out, not_1_out);  // AND_Gate
  or or_1 (out_3, and_1_out, and_2_out);

  assign in3 = in2;

  // Notes on the sheet:
  //   Recitation 6, Task 4
  //   !2&!3
  //   2&3
  //   2&3 | !2&!3
endmodule
