// Logisim project Task1+2.circ as structural Verilog: 1 circuit, main circuit main
module main (
  input  A,
  input  B,
  input  [15:0] in16Bits,
  output out,
  output [15:0] out16Bits
);

  // Probe on B
  and and_1 (out, A, B);
  assign out16Bits[7:0] = ~in16Bits[7:0];  // NOT_Gate not_1, 8 bits wide
  assign out16Bits[15:8] = ~in16Bits[15:8];  // NOT_Gate not_2, 8 bits wide

  // Other names for the same wires on the sheet: tunnel = out

  // Notes on the sheet:
  //   Bus
  //   Probe
  //   Splitter
  //   Wide NOT Gate
  //   Tunnel
endmodule
