// Logisim project Task3.circ as structural Verilog: 1 circuit, main circuit main
module main (
  input  [5:0] \input ,
  output RWE,
  output [1:0] ALUop,
  output DWE,
  output MuxA
);

  wire add_out, lw_out, not_1_out, not_2_out, not_3_out, not_4_out, not_5_out, not_6_out, not_7_out,
       not_8_out, not_9_out, not_10_out, not_11_out, not_12_out, not_13_out, not_14_out, not_15_out, sub_out;

  not not_1 (not_1_out, \input [1]);
  not not_2 (not_2_out, \input [3]);
  not not_3 (not_3_out, \input [5]);
  not not_4 (not_4_out, \input [4]);
  not not_5 (not_5_out, \input [3]);
  not not_6 (not_6_out, \input [2]);
  not not_7 (not_7_out, \input [4]);
  not not_8 (not_8_out, \input [0]);
  not not_9 (not_9_out, \input [1]);
  not not_10 (not_10_out, \input [0]);
  not not_11 (not_11_out, \input [1]);
  not not_12 (not_12_out, \input [3]);
  not not_13 (not_13_out, \input [4]);
  not not_14 (not_14_out, \input [1]);
  not not_15 (not_15_out, \input [2]);
  and add (add_out, \input [0], not_1_out, not_2_out, not_7_out, not_3_out);
  and sub (sub_out, \input [0], \input [1], not_2_out, not_7_out, not_3_out);
  and sw (DWE, not_8_out, not_9_out, \input [2], \input [4], \input [5]);
  and lw (lw_out, not_10_out, not_11_out, not_12_out, not_13_out, \input [5]);
  and beq (ALUop[1], \input [0], not_14_out, not_5_out, not_4_out, \input [5]);
  or add_sub_lw (RWE, add_out, sub_out, lw_out);
  or sub_beq (ALUop[0], sub_out, ALUop[1]);
  or sw_lw (MuxA, DWE, lw_out);
endmodule
