// Logisim project Tasks.circ as structural Verilog: 4 circuits, main circuit main
module main (
  input  rwe,
  input  [1:0] op,
  input  reset,
  input  rdst,
  input  [2:0] rd,
  input  [2:0] rt,
  input  [2:0] rs
);

  wire clk, not_1_out;
  wire [2:0] multiplexer_1_out;
  wire [15:0] ALU_outputdata, RegFile_s, RegFile_t;

  Clock clock_1 (.out(clk));
  not not_1 (not_1_out, clk);
  Multiplexer #(.width(3), .enable("false")) multiplexer_1 (.in0(rd), .in1(rt), .out(multiplexer_1_out), .sel(rdst));
  RegFile RegFile (
    .D(ALU_outputdata), .WE(rwe), .rs(rs), .clk(not_1_out), .rst(reset), .rt(rt), .rd(multiplexer_1_out),
    .s(RegFile_s), .t(RegFile_t));
  ALU ALU (.InputData1(RegFile_s), .InputData2(RegFile_t), .OpType(op), .OutputData(ALU_outputdata));
endmodule

module RegFile (
  input  [15:0] D,
  input  WE,
  input  [2:0] rs,
  input  clk,
  input  rst,
  input  [2:0] rt,
  input  [2:0] rd,
  output [15:0] s,
  output [15:0] t
);

  wire _1, _2, _3, _4, _5, _6, _7, and_1_out, and_2_out, and_3_out, and_4_out, and_5_out, and_6_out,
       and_7_out;
  wire [15:0] r0, r1, r2, r3, r4, r5, r6, r7;

  Decoder #(.select(3)) decoder_1 (
    .out1(_1), .out2(_2), .out3(_3), .out4(_4), .out5(_5), .out6(_6), .out7(_7), .sel(rd));  // open: out0, en
  SingleReg singlereg_1 (.\input (D), .Reset(rst), .Enable(1'b0), .\output (r0), .clk(clk));
  and and_1 (and_1_out, WE, _1);
  and and_2 (and_2_out, WE, _2);
  and and_3 (and_3_out, WE, _3);
  and and_4 (and_4_out, WE, _4);
  and and_5 (and_5_out, WE, _5);
  and and_6 (and_6_out, WE, _6);
  and and_7 (and_7_out, WE, _7);
  SingleReg singlereg_2 (.\input (D), .Reset(rst), .Enable(and_1_out), .\output (r1), .clk(clk));
  SingleReg singlereg_3 (.\input (D), .Reset(rst), .Enable(and_2_out), .\output (r2), .clk(clk));
  SingleReg singlereg_4 (.\input (D), .Reset(rst), .Enable(and_3_out), .\output (r3), .clk(clk));
  SingleReg singlereg_5 (.\input (D), .Reset(rst), .Enable(and_4_out), .\output (r4), .clk(clk));
  SingleReg singlereg_6 (.\input (D), .Reset(rst), .Enable(and_5_out), .\output (r5), .clk(clk));
  SingleReg singlereg_7 (.\input (D), .Reset(rst), .Enable(and_6_out), .\output (r6), .clk(clk));
  SingleReg singlereg_8 (.\input (D), .Reset(rst), .Enable(and_7_out), .\output (r7), .clk(clk));
  // Probe on r0
  // Probe on r1
  // Probe on r2
  // Probe on r3
  Multiplexer #(.select(3), .width(16), .enable("false")) multiplexer_1 (
    .in0(r0), .in1(r1), .in2(r2), .in3(r3), .in4(r4), .in5(r5), .in6(r6), .in7(r7), .out(s), .sel(rs));
  Multiplexer #(.select(3), .width(16), .enable("false")) multiplexer_2 (
    .in0(r0), .in1(r1), .in2(r2), .in3(r3), .in4(r4), .in5(r5), .in6(r6), .in7(r7), .out(t), .sel(rt));
  // Probe on r4
  // Probe on r5
  // Probe on r6
  // Probe on r7

  // Notes on the sheet:
  //   DECODER: only 1 output not equal 0
endmodule

module ALU (
  input  [15:0] InputData1,
  input  [15:0] InputData2,
  input  [1:0] OpType,
  output [15:0] OutputData
);

  wire [15:0] adder_1_out, NAND_out, subtractor_1_out, XOR_out;

  Adder #(.width(16)) adder_1 (.a(InputData1), .b(InputData2), .out(adder_1_out));  // open: cin, cout
  Subtractor #(.width(16)) subtractor_1 (.a(InputData1), .b(InputData2), .out(subtractor_1_out));  // open: bin, bout
  assign XOR_out = InputData1 ^ InputData2;  // XOR_Gate XOR, 16 bits wide
  assign NAND_out = ~(InputData1 & InputData2);  // NAND_Gate NAND, 16 bits wide
  Multiplexer #(.select(2), .width(16)) multiplexer_1 (
    .in0(adder_1_out), .in1(subtractor_1_out), .in3(XOR_out), .out(OutputData), .sel(OpType));  // open: in2, en
endmodule

module SingleReg (
  input  clk,
  input  [15:0] \input ,
  input  Reset,
  input  Enable,
  output [15:0] \output 
);

  D_Flip_Flop d_ff_1 (.clk(clk), .D(\input [0]), .Q(\output [0]), .en(Enable), .reset(Reset));  // open: Qn, preset
  D_Flip_Flop d_ff_2 (.clk(clk), .D(\input [1]), .Q(\output [1]), .en(Enable), .reset(Reset));  // open: Qn, preset
  D_Flip_Flop d_ff_3 (.clk(clk), .D(\input [2]), .Q(\output [2]), .en(Enable), .reset(Reset));  // open: Qn, preset
  D_Flip_Flop d_ff_4 (.clk(clk), .D(\input [3]), .Q(\output [3]), .en(Enable), .reset(Reset));  // open: Qn, preset
  D_Flip_Flop d_ff_5 (.clk(clk), .D(\input [4]), .Q(\output [4]), .en(Enable), .reset(Reset));  // open: Qn, preset
  D_Flip_Flop d_ff_6 (.clk(clk), .D(\input [5]), .Q(\output [5]), .en(Enable), .reset(Reset));  // open: Qn, preset
  D_Flip_Flop d_ff_7 (.clk(clk), .D(\input [6]), .Q(\output [6]), .en(Enable), .reset(Reset));  // open: Qn, preset
  D_Flip_Flop d_ff_8 (.clk(clk), .D(\input [7]), .Q(\output [7]), .en(Enable), .reset(Reset));  // open: Qn, preset
  D_Flip_Flop d_ff_9 (.clk(clk), .D(\input [8]), .Q(\output [8]), .en(Enable), .reset(Reset));  // open: Qn, preset
  D_Flip_Flop d_ff_10 (.clk(clk), .D(\input [9]), .Q(\output [9]), .en(Enable), .reset(Reset));  // open: Qn, preset
  D_Flip_Flop d_ff_11 (.clk(clk), .D(\input [10]), .Q(\output [10]), .en(Enable), .reset(Reset));  // open: Qn, preset
  D_Flip_Flop d_ff_12 (.clk(clk), .D(\input [11]), .Q(\output [11]), .en(Enable), .reset(Reset));  // open: Qn, preset
  D_Flip_Flop d_ff_13 (.clk(clk), .D(\input [12]), .Q(\output [12]), .en(Enable), .reset(Reset));  // open: Qn, preset
  D_Flip_Flop d_ff_14 (.clk(clk), .D(\input [13]), .Q(\output [13]), .en(Enable), .reset(Reset));  // open: Qn, preset
  D_Flip_Flop d_ff_15 (.clk(clk), .D(\input [14]), .Q(\output [14]), .en(Enable), .reset(Reset));  // open: Qn, preset
  D_Flip_Flop d_ff_16 (.clk(clk), .D(\input [15]), .Q(\output [15]), .en(Enable), .reset(Reset));  // open: Qn, preset

  // Other names for the same wires on the sheet: in0 = \input [0]; in1 = \input [1]; in2 = \input [2];
  //   in3 = \input [3]; in4 = \input [4]; in5 = \input [5]; in6 = \input [6]; in7 = \input [7]; in8 = \input [8];
  //   in9 = \input [9]; in10 = \input [10]; in11 = \input [11]; in12 = \input [12]; in13 = \input [13];
  //   in14 = \input [14]; in15 = \input [15]; _0 = \output [0]; _1 = \output [1]; _2 = \output [2]; _3 = \output [3];
  //   _4 = \output [4]; _5 = \output [5]; _6 = \output [6]; _7 = \output [7]; _8 = \output [8]; _9 = \output [9];
  //   _10 = \output [10]; _11 = \output [11]; _12 = \output [12]; _13 = \output [13]; _14 = \output [14];
  //   _15 = \output [15]
endmodule
